// Logisim project regfile.circ as structural Verilog: 1 circuit, main circuit main
module main (
  input  [4:0] rs1,
  input  [4:0] rs2,
  input  [4:0] rd,
  input  [31:0] Write_Data,
  input  RegWEn,
  input  clk,
  output [31:0] ra,
  output [31:0] sp,
  output [31:0] t0,
  output [31:0] t1,
  output [31:0] t2,
  output [31:0] s0,
  output [31:0] s1,
  output [31:0] a0,
  output [31:0] Read_Data_1,
  output [31:0] Read_Data_2
);

  wire a0_WE, ra_WE, s0_WE, s1_WE, sp_WE, t0_WE, t1_WE, t2_WE;
  wire [31:0] a0_DA, ra_DA, s0_DA, s1_DA, sp_DA, t0_DA, t1_DA, t2_DA, ze_DA, zero;

  Demultiplexer #(.select(5), .enable("false")) demultiplexer_1 (
    .out1(ra_WE), .out2(sp_WE), .out5(t0_WE), .out6(t1_WE), .out7(t2_WE), .out8(s0_WE), .out9(s1_WE),
    .out10(a0_WE), .in(RegWEn), .sel(rd));  // open: out0, out3, out4, out11, out12, out13, out14, out15, out16, out17, out18, out19, out20, out21, out22, out23, out24, out25, out26, out27, out28, out29, out30, out31
  Demultiplexer #(.select(5), .width(32), .enable("false")) demultiplexer_2 (
    .out0(ze_DA), .out1(ra_DA), .out2(sp_DA), .out5(t0_DA), .out6(t1_DA), .out7(t2_DA), .out8(s0_DA),
    .out9(s1_DA), .out10(a0_DA), .in(Write_Data), .sel(rd));  // open: out3, out4, out11, out12, out13, out14, out15, out16, out17, out18, out19, out20, out21, out22, out23, out24, out25, out26, out27, out28, out29, out30, out31
  Register #(.width(32)) register_1 (.D(ra_DA), .en(ra_WE), .clk(clk), .Q(ra));  // open: clr
  Register #(.width(32)) register_2 (.D(sp_DA), .en(sp_WE), .clk(clk), .Q(sp));  // open: clr
  Register #(.width(32)) register_3 (.D(t0_DA), .en(t0_WE), .clk(clk), .Q(t0));  // open: clr
  Register #(.width(32)) register_4 (.D(t1_DA), .en(t1_WE), .clk(clk), .Q(t1));  // open: clr
  Register #(.width(32)) register_5 (.D(t2_DA), .en(t2_WE), .clk(clk), .Q(t2));  // open: clr
  Register #(.width(32)) register_6 (.D(s0_DA), .en(s0_WE), .clk(clk), .Q(s0));  // open: clr
  Register #(.width(32)) register_7 (.D(ze_DA), .en(1'b0), .clk(clk), .Q(zero));  // open: clr
  Register #(.width(32)) register_8 (.D(a0_DA), .en(a0_WE), .clk(clk), .Q(a0));  // open: clr
  Register #(.width(32)) register_9 (.D(s1_DA), .en(s1_WE), .clk(clk), .Q(s1));  // open: clr
  Multiplexer #(.select(5), .width(32), .enable("false")) multiplexer_1 (
    .in0(zero), .in1(ra), .in2(sp), .in5(t0), .in6(t1), .in7(t2), .in8(s0), .in9(s1), .in10(a0),
    .out(Read_Data_1), .sel(rs1));  // open: in3, in4, in11, in12, in13, in14, in15, in16, in17, in18, in19, in20, in21, in22, in23, in24, in25, in26, in27, in28, in29, in30, in31
  Multiplexer #(.select(5), .width(32), .enable("false")) multiplexer_2 (
    .in0(zero), .in1(ra), .in2(sp), .in5(t0), .in6(t1), .in7(t2), .in8(s0), .in9(s1), .in10(a0),
    .out(Read_Data_2), .sel(rs2));  // open: in3, in4, in11, in12, in13, in14, in15, in16, in17, in18, in19, in20, in21, in22, in23, in24, in25, in26, in27, in28, in29, in30, in31

  // Other names for the same wires on the sheet: read_data1[31:0] = Read_Data_1; read_data2[31:0] = Read_Data_2;
  //   read_reg1[4:0] = rs1; read_reg2[4:0] = rs2; write_en = RegWEn; write_reg[4:0] = rd

  // Notes on the sheet:
  //   INPUTS to your circuit
  //   DON'T CHANGE THE LOCATIONS OF THE INPUTS AND OUTPUTS!
  //   These are DEBUG/TEST outputs from your circuit.
  //   OUTPUTS from your circuit
endmodule
