// Logisim project alu.circ as structural Verilog: 4 circuits, main circuit alu
module alu (
  input  [31:0] A,
  input  [31:0] B,
  input  [3:0] ALUSel,
  output [31:0] Result
);

  wire comparator_2_eq, comparator_3_eq, comparator_4_eq;
  wire [0:0] SLT_10;
  wire [5:0] bitadder_1_out, bitadder_2_out, CNTO_13;
  wire [15:0] lidanglaoshi_1_out_2, lidanglaoshi_1_out_3, lidanglaoshi_2_out_2, lidanglaoshi_2_out_3;
  wire [31:0] ADD_0, AND_6, bit_extender_1_out, bit_extender_2_out, BITPAL_14, DIVU_4, MULH_2, MULT_3,
       MULT_U, OR_7, REMU_5, shilaodangli_1_out_2, SIR_15, SLL_9, SRA_11, SRL_12, SUB_1, XOR_8;

  assign AND_6 = A & B;  // AND_Gate and_1, 32 bits wide
  assign OR_7 = A | B;  // OR_Gate or_1, 32 bits wide
  assign XOR_8 = A ^ B;  // XOR_Gate xor_1, 32 bits wide
  Shifter #(.width(32)) shifter_1 (.in(A), .\dist (B[4:0]), .out(SLL_9));
  Comparator #(.width(32)) comparator_1 (.a(A), .b(B), .lt(SLT_10[0]));  // open: gt, eq
  Shifter #(.width(32), .shift("ar")) shifter_2 (.in(A), .\dist (B[4:0]), .out(SRA_11));
  Shifter #(.width(32), .shift("lr")) shifter_3 (.in(A), .\dist (B[4:0]), .out(SRL_12));
  BitAdder #(.width(32)) bitadder_1 (.in0(A), .out(bitadder_1_out));
  BitAdder #(.width(32)) bitadder_2 (.in0(B), .out(bitadder_2_out));
  Adder #(.width(6)) adder_1 (.a(bitadder_1_out), .b(bitadder_2_out), .out(CNTO_13));  // open: cin, cout
  // Probe on A
  // Probe on B
  // Probe on ADD_0
  Adder #(.width(32)) adder_2 (.a(A), .b(B), .out(ADD_0));  // open: cin, cout
  Subtractor #(.width(32)) subtractor_1 (.a(A), .b(B), .out(SUB_1));  // open: bin, bout
  Multiplier #(.width(32)) multiplier_1 (.a(A), .b(B), .out(MULT_3), .cout(MULT_U));  // open: cin
  Divider #(.width(32)) divider_1 (.a(A), .b(B), .out(DIVU_4), .rem(REMU_5));  // open: upper
  lidanglaoshi lidanglaoshi_1 (.in_1(A), .out_2(lidanglaoshi_1_out_2), .out_3(lidanglaoshi_1_out_3));
  lidanglaoshi lidanglaoshi_2 (.in_1(B), .out_2(lidanglaoshi_2_out_2), .out_3(lidanglaoshi_2_out_3));
  MULH mulh_1 (.in_1(A), .in_2(B), .out_3(MULH_2));
  shilaodangli shilaodangli_1 (.in_1(B), .out_2(shilaodangli_1_out_2));
  Comparator #(.width(16)) comparator_2 (
    .a(lidanglaoshi_1_out_2), .b(lidanglaoshi_1_out_3), .eq(comparator_2_eq));  // open: gt, lt
  Comparator #(.width(16)) comparator_3 (
    .a(lidanglaoshi_2_out_2), .b(lidanglaoshi_2_out_3), .eq(comparator_3_eq));  // open: gt, lt
  Comparator #(.width(32)) comparator_4 (.a(A), .b(shilaodangli_1_out_2), .eq(comparator_4_eq));  // open: gt, lt
  assign bit_extender_1_out = {{31{1'b0}}, comparator_2_eq};  // Bit_Extender bit_extender_1
  assign bit_extender_2_out = {{31{1'b0}}, comparator_3_eq};  // Bit_Extender bit_extender_2
  assign BITPAL_14 = bit_extender_1_out | bit_extender_2_out;  // OR_Gate or_2, 32 bits wide
  assign SIR_15 = {{31{1'b0}}, comparator_4_eq};  // Bit_Extender bit_extender_3
  // Probe on Result
  Multiplexer #(.select(4), .width(32), .enable("false")) multiplexer_1 (
    .in0(AND_6), .in1(OR_7), .in2(XOR_8), .in3(ADD_0), .in4(SUB_1), .in5(MULT_3), .in6(MULT_U), .in7(MULH_2),
    .in8(DIVU_4), .in9(REMU_5), .in10(SRL_12), .in11(SRA_11), .in12(SLL_9), .in13({{31{1'b0}}, SLT_10[0]}),
    .in14({{26{1'b0}}, CNTO_13}), .in15(SIR_15), .out(Result), .sel(ALUSel));

  // Notes on the sheet:
  //   INPUTS to your circuit
  //   DON'T CHANGE THE LOCATIONS OF THE INPUTS AND OUTPUTS!
  //   OUTPUT from your circuit
endmodule

module shilaodangli (
  input  [31:0] in_1,
  output [31:0] out_2
);


  assign out_2 = {in_1[0], in_1[1], in_1[2], in_1[3], in_1[4], in_1[5], in_1[6], in_1[7], in_1[8], in_1[9], in_1[10], in_1[11], in_1[12], in_1[13], in_1[14], in_1[15], in_1[16], in_1[17], in_1[18], in_1[19], in_1[20], in_1[21], in_1[22], in_1[23], in_1[24], in_1[25], in_1[26], in_1[27], in_1[28], in_1[29], in_1[30], in_1[31]};
endmodule

module lidanglaoshi (
  input  [31:0] in_1,
  output [15:0] out_2,
  output [15:0] out_3
);


  assign out_2 = {in_1[0], in_1[1], in_1[2], in_1[3], in_1[4], in_1[5], in_1[6], in_1[7], in_1[8], in_1[9], in_1[10], in_1[11], in_1[12], in_1[13], in_1[14], in_1[15]};
  assign out_3 = in_1[31:16];
endmodule

module MULH (
  input  [31:0] in_1,
  input  [31:0] in_2,
  output [31:0] out_3
);

  wire [31:0] CASE_00, CASE_01, CASE_10, CASE_11, negator_1_out, negator_2_out;

  Negator #(.width(32)) negator_1 (.in(in_1), .out(negator_1_out));
  Negator #(.width(32)) negator_2 (.in(in_2), .out(negator_2_out));
  Multiplier #(.width(32)) multiplier_1 (.a(in_2), .b({32{1'b1}}), .out(CASE_01), .cin(CASE_00));  // open: cout
  Multiplier #(.width(32)) multiplier_2 (.a(negator_1_out), .b(negator_2_out), .cout(CASE_11));  // open: out, cin
  Multiplier #(.width(32)) multiplier_3 (.a(in_1), .b(in_2), .cout(CASE_00));  // open: out, cin
  Multiplier #(.width(32)) multiplier_4 (.a(in_1), .b({32{1'b1}}), .out(CASE_10), .cin(CASE_00));  // open: cout
  Multiplexer #(.select(2), .width(32), .enable("false")) multiplexer_1 (
    .in0(CASE_00), .in1(CASE_01), .in2(CASE_10), .in3(CASE_11), .out(out_3), .sel({in_2[31], in_1[31]}));

  // Other names for the same wires on the sheet: A[31:0] = in_1; A_sign = in_1[31]; B[31:0] = in_2; B_sign = in_2[31]
endmodule
