// Logisim project cpu.circ as structural Verilog: 3 circuits, main circuit main
module main (
  input  [31:0] INSTRUCTION,
  input  in_2,
  output [31:0] FETCH_ADDRESS,
  output [31:0] ra,
  output [31:0] sp,
  output [31:0] t0,
  output [31:0] t1,
  output [31:0] t2,
  output [31:0] s0,
  output [31:0] s1,
  output [31:0] a0
);

  wire ASel, BrEq, BrLt, BrUn, BSel, clock_1_out, lbu, lh, lhu, lw, MemRW, PCSel, RegWEn;
  wire [1:0] WBSel;
  wire [2:0] ImmSel;
  wire [3:0] ALUSel;
  wire [4:0] imm_S;
  wire [6:0] INSTRUCTION_1;
  wire [19:12] imm_U;
  wire [31:0] bit_extender_1_out, bit_extender_2_out, bit_extender_3_out, bit_extender_4_out, imm,
       imm_I_0x67, multiplexer_1_out, multiplexer_3_out, multiplexer_4_out, multiplexer_5_out,
       multiplexer_6_out, multiplexer_7_out, multiplexer_8_out, PC, PC_p_p_4, PC_PLUS_4, PC_q, RAM_output,
       ReadData, Result, rs1, rs2, shifter_2_out, undriven, WriteBack;
  wire [31:5] imm_I_0x_3;

  // Probe on {imm_I_0x_3[31], imm_I_0x_3[10:5], imm_I_0x67[31], imm_I_0x67[3:0], imm_U, imm_S, INSTRUCTION_1}
  Multiplexer #(.width(32), .enable("false")) multiplexer_1 (
    .in0(PC_PLUS_4), .in1(Result), .out(multiplexer_1_out), .sel(PCSel));
  // Probe on INSTRUCTION
  // Probe on FETCH_ADDRESS
  Adder #(.width(32)) adder_1 (.a(PC_q), .b(32'h4), .out(PC_PLUS_4));  // open: cin, cout
  Register #(.width(32)) u_PC (.D(multiplexer_1_out), .clk(in_2), .Q(PC_q));  // open: en, clr
  Clock clock_1 (.out(clock_1_out));
  Register #(.width(32)) register_1 (.D(PC_q), .clk(in_2), .Q(PC));  // open: en, clr
  Shifter #(.width(32), .shift("lr")) shifter_1 (.in(PC_q), .\dist (5'b00010), .out(FETCH_ADDRESS));
  Multiplexer #(.select(3), .width(32), .enable("false")) multiplexer_2 (
    .in0({{21{imm_I_0x_3[31]}}, imm_I_0x_3[10:5], imm_I_0x67[31], imm_I_0x67[3:0]}),
    .in1({{21{imm_I_0x_3[31]}}, imm_I_0x_3[10:5], imm_S}),
    .in2({{20{imm_I_0x_3[31]}}, imm_S[0], imm_I_0x_3[10:5], imm_S[4:1], 1'b0}),
    .in3({imm_I_0x_3[31], imm_I_0x_3[10:5], imm_I_0x67[31], imm_I_0x67[3:0], imm_U, {12{1'b0}}}),
    .in4({{12{imm_I_0x_3[31]}}, imm_U, imm_I_0x67[0], imm_I_0x_3[10:5], imm_I_0x67[31], imm_I_0x67[3:1], 1'b0}),
    .in5({{28{imm_I_0x67[31]}}, imm_I_0x67[3:0]}), .out(imm), .sel(ImmSel));  // open: in6, in7
  Multiplexer #(.width(32), .enable("false")) multiplexer_3 (
    .in0(INSTRUCTION), .in1(32'h13), .out(multiplexer_3_out), .sel(PCSel));
  Adder #(.width(32)) adder_2 (.a(PC), .b(32'h4), .out(PC_p_p_4));  // open: cin, cout
  Register #(.width(32)) register_2 (
    .D(multiplexer_3_out), .clk(in_2),
    .Q({imm_I_0x_3[31], imm_I_0x_3[10:5], imm_I_0x67[31], imm_I_0x67[3:0], imm_U, imm_S, INSTRUCTION_1}));  // open: en, clr
  // Probe on imm
  // Probe on {imm_I_0x_3[31], imm_I_0x_3[10:5], imm_I_0x67[31], imm_I_0x67[3:0], imm_U, imm_S, INSTRUCTION_1}
  regfile_main RegFile (
    .rs2({imm_I_0x67[31], imm_I_0x67[3:0]}), .rd(imm_S), .Read_Data_1(rs1), .Read_Data_2(rs2), .ra(ra),
    .sp(sp), .t0(t0), .t1(t1), .t2(t2), .s0(s0), .s1(s1), .a0(a0), .rs1(imm_U[19:15]),
    .Write_Data(WriteBack), .RegWEn(RegWEn), .clk(in_2));
  control_logic control_logic_1 (
    .BrEq(BrEq), .BrLt(BrLt),
    .Instructions({imm_I_0x_3[31], imm_I_0x_3[10:5], imm_I_0x67[31], imm_I_0x67[3:0], imm_U, imm_S, INSTRUCTION_1}),
    .lhu(lhu), .lw(lw), .lbu(lbu), .lh(lh), .PCSel(PCSel), .RegWEn(RegWEn), .ImmSel(ImmSel), .BrUn(BrUn),
    .ASel(ASel), .BSel(BSel), .ALUSel(ALUSel), .MemRW(MemRW), .WBSel(WBSel));
  // Probe on multiplexer_5_out
  // Probe on multiplexer_4_out
  Multiplexer #(.width(32), .enable("false")) multiplexer_4 (.in0(rs1), .in1(PC), .out(multiplexer_4_out), .sel(ASel));
  Multiplexer #(.width(32), .enable("false")) multiplexer_5 (.in0(rs2), .in1(imm), .out(multiplexer_5_out), .sel(BSel));
  alu Arithmetic_Logic_Unit (.A(multiplexer_4_out), .B(multiplexer_5_out), .ALUSel(ALUSel), .Result(Result));
  branch branch_1 (.RS1(rs1), .RS2(rs2), .BrUn(BrUn), .BrEq(BrEq), .BrLt(BrLt));
  // Probe on ImmSel
  // Probe on BSel
  // Probe on MemRW
  // Probe on WBSel
  // Probe on Result
  Shifter #(.width(32), .shift("lr")) shifter_2 (.in(Result), .\dist (5'b00010), .out(shifter_2_out));
  // Probe on BrUn
  // Probe on PCSel
  // Probe on ALUSel
  assign bit_extender_1_out = {{24{1'b0}}, RAM_output[7:0]};  // Bit_Extender bit_extender_1
  assign bit_extender_2_out = {{24{RAM_output[7]}}, RAM_output[7:0]};  // Bit_Extender bit_extender_2
  assign bit_extender_3_out = {{16{RAM_output[15]}}, RAM_output[15:0]};  // Bit_Extender bit_extender_3
  assign bit_extender_4_out = {{16{1'b0}}, RAM_output[15:0]};  // Bit_Extender bit_extender_4
  Multiplexer #(.width(32), .enable("false")) multiplexer_6 (
    .in0(bit_extender_2_out), .in1(bit_extender_3_out), .out(multiplexer_6_out), .sel(lh));
  mem_main DMEM (.clock(in_2), .Write_enable(MemRW), .Addr(shifter_2_out), .Read(RAM_output), .Write(rs2));
  Multiplexer #(.width(32), .enable("false")) multiplexer_7 (
    .in0(multiplexer_6_out), .in1(RAM_output), .out(multiplexer_7_out), .sel(lw));
  Multiplexer #(.width(32), .enable("false")) multiplexer_8 (
    .in0(multiplexer_7_out), .in1(bit_extender_1_out), .out(multiplexer_8_out), .sel(lbu));
  Multiplexer #(.width(32), .enable("false")) multiplexer_9 (
    .in0(multiplexer_8_out), .in1(bit_extender_4_out), .out(ReadData), .sel(lhu));
  // Probe on ReadData
  Multiplexer #(.select(2), .width(32), .enable("false")) multiplexer_10 (
    .in0(ReadData), .in1(Result), .in2(PC_p_p_4), .in3(undriven), .out(WriteBack), .sel(WBSel));

  // Other names for the same wires on the sheet: clk = in_2; fetch_addr[31:0] = FETCH_ADDRESS;
  //   imm_I_0x_3 (some bits) = {{20{imm_I_0x_3[31]}}, imm_I_0x67[31], imm_I_0x67[3:0]};
  //   imm_U[31:20] = {imm_I_0x_3[31], imm_I_0x_3[10:5], imm_I_0x67[31], imm_I_0x67[3:0]};
  //   imm_UJ[31:1] = {{12{imm_I_0x_3[31]}}, imm_U, imm_I_0x67[0], imm_I_0x_3[10:5], imm_I_0x67[31], imm_I_0x67[3:1]};
  //   INSTRUCTION_1[31:7] = {imm_I_0x_3[31], imm_I_0x_3[10:5], imm_I_0x67[31], imm_I_0x67[3:0], imm_U, imm_S};
  //   imm_I_0x67[30:4] = {27{imm_I_0x67[31]}};
  //   imm_SB[31:1] = {{20{imm_I_0x_3[31]}}, imm_S[0], imm_I_0x_3[10:5], imm_S[4:1]};
  //   imm_S[31:5] = {{21{imm_I_0x_3[31]}}, imm_I_0x_3[10:5]}

  // Notes on the sheet:
  //   Output
  //   IMM
  //   Inputs/Outputs from run.circ. DO NOT MOVE THESE.
  //   ERR
  //   Inputs
  //   It is OK to move the PC, RegFile, ALU, and MEM to wherever is most convenient for you when constructing your CPU, and to delete this text
  //   Inputs/Outputs from run.circ. DO NOT MOVE THESE.
  //   pay attention to MemRW and WriteDAta - Apperence
endmodule

module branch (
  input  [31:0] RS1,
  input  [31:0] RS2,
  input  BrUn,
  output BrEq,
  output BrLt
);

  wire BrEq_s, BrEq_u, BrLt_s, BrLt_u;

  Comparator #(.width(32)) comparator_1 (.a(RS1), .b(RS2), .eq(BrEq_s), .lt(BrLt_s));  // open: gt
  Comparator #(.width(32), .mode("unsigned")) comparator_2 (.a(RS1), .b(RS2), .eq(BrEq_u), .lt(BrLt_u));  // open: gt
  Multiplexer #(.enable("false")) multiplexer_1 (.in0(BrEq_s), .in1(BrEq_u), .out(BrEq), .sel(BrUn));
  Multiplexer #(.enable("false")) multiplexer_2 (.in0(BrLt_s), .in1(BrLt_u), .out(BrLt), .sel(BrUn));
endmodule

module control_logic (
  input  BrEq,
  input  BrLt,
  input  [31:0] Instructions,
  output lhu,
  output lw,
  output lbu,
  output lh,
  output PCSel,
  output RegWEn,
  output [2:0] ImmSel,
  output BrUn,
  output ASel,
  output BSel,
  output [3:0] ALUSel,
  output MemRW,
  output [1:0] WBSel
);

  wire add, addi, ALU, and1, andi, auipc, B, beq, beq_t, bgeu, bgeu_t, blt, blt_t, bltu, bltu_t, bne, bne_t,
       comparator_10_eq, comparator_11_eq, comparator_12_eq, comparator_13_eq, comparator_14_eq,
       comparator_15_eq, comparator_16_eq, comparator_17_eq, comparator_18_eq, comparator_19_eq,
       comparator_20_eq, comparator_21_eq, comparator_22_eq, comparator_23_eq, comparator_24_eq,
       comparator_25_eq, comparator_26_eq, comparator_27_eq, comparator_28_eq, comparator_29_eq,
       comparator_30_eq, comparator_31_eq, comparator_32_eq, comparator_33_eq, comparator_34_eq,
       comparator_35_eq, comparator_36_eq, comparator_37_eq, comparator_38_eq, comparator_39_eq,
       comparator_40_eq, comparator_41_eq, comparator_42_eq, comparator_43_eq, comparator_44_eq,
       comparator_45_eq, comparator_46_eq, comparator_47_eq, comparator_48_eq, comparator_49_eq,
       comparator_50_eq, comparator_51_eq, comparator_52_eq, comparator_53_eq, comparator_54_eq,
       comparator_55_eq, comparator_56_eq, comparator_57_eq, comparator_58_eq, comparator_59_eq, divu, I,
       Imm, Ioad, J, lb, lui, mulh, mulhu, mult, not_3_out, not_4_out, or1, or_1_out, or_2_out, or_4_out,
       or_5_out, or_8_out, or_9_out, or_10_out, or_11_out, or_12_out, or_13_out, or_14_out, or_15_out,
       or_16_out, ori, R, remu, S, sll1, slli, slt1, slti, sra1, srai, srl1, srli, sub, xor1, xori;
  wire [1:0] multiplexer_13_out, multiplexer_18_out;
  wire [2:0] multiplexer_12_out, multiplexer_15_out, multiplexer_17_out, multiplexer_19_out,
       multiplexer_22_out;
  wire [3:0] multiplexer_1_out, multiplexer_2_out, multiplexer_3_out, multiplexer_4_out, multiplexer_5_out,
       multiplexer_6_out, multiplexer_7_out, multiplexer_8_out, multiplexer_9_out, multiplexer_10_out,
       multiplexer_11_out, multiplexer_14_out;

  // Probe on Instructions[6:0]
  Comparator #(.width(7), .mode("unsigned")) comparator_1 (
    .a(Instructions[6:0]), .b(7'b0110011), .eq(R));  // open: gt, lt
  Comparator #(.width(7), .mode("unsigned")) comparator_2 (
    .a(Instructions[6:0]), .b(7'b0000011), .eq(Ioad));  // open: gt, lt
  Comparator #(.width(7), .mode("unsigned")) comparator_3 (
    .a(Instructions[6:0]), .b(7'b0010011), .eq(Imm));  // open: gt, lt
  Comparator #(.width(7), .mode("unsigned")) comparator_4 (
    .a(Instructions[6:0]), .b(7'b0100011), .eq(S));  // open: gt, lt
  Comparator #(.width(7), .mode("unsigned")) comparator_5 (
    .a(Instructions[6:0]), .b(7'b1100011), .eq(B));  // open: gt, lt
  Comparator #(.width(7), .mode("unsigned")) comparator_6 (
    .a(Instructions[6:0]), .b(7'b0110111), .eq(lui));  // open: gt, lt
  Comparator #(.width(7), .mode("unsigned")) comparator_7 (
    .a(Instructions[6:0]), .b(7'b0010111), .eq(auipc));  // open: gt, lt
  Comparator #(.width(7), .mode("unsigned")) comparator_8 (
    .a(Instructions[6:0]), .b(7'b1101111), .eq(J));  // open: gt, lt
  Comparator #(.width(7), .mode("unsigned")) comparator_9 (
    .a(Instructions[6:0]), .b(7'b1100111), .eq(I));  // open: gt, lt
  or or_1 (or_1_out, or1, ori);
  or or_2 (or_2_out, beq, bne, blt, MemRW, bgeu, bltu);
  or or_3 (ASel, beq, bne, blt, bltu, bgeu, J, auipc);
  Multiplexer #(.width(4), .enable("false")) multiplexer_1 (
    .in0(4'b0000), .in1(4'b0001), .out(multiplexer_1_out), .sel(or_1_out));
  // Probe on Instructions
  not not_1 (RegWEn, or_2_out);
  Multiplexer #(.width(4), .enable("false")) multiplexer_2 (
    .in0(multiplexer_1_out), .in1(4'b0010), .out(multiplexer_2_out), .sel(or_4_out));
  or or_4 (or_4_out, xor1, xori);
  Comparator #(.width(3), .mode("unsigned")) comparator_10 (
    .a(Instructions[14:12]), .b(3'b000), .eq(comparator_10_eq));  // open: gt, lt
  Comparator #(.width(7), .mode("unsigned")) comparator_11 (
    .a(Instructions[31:25]), .b({7{1'b0}}), .eq(comparator_11_eq));  // open: gt, lt
  Comparator #(.width(3), .mode("unsigned")) comparator_12 (
    .a(Instructions[14:12]), .b(3'b001), .eq(comparator_12_eq));  // open: gt, lt
  Comparator #(.width(7), .mode("unsigned")) comparator_13 (
    .a(Instructions[31:25]), .b({7{1'b0}}), .eq(comparator_13_eq));  // open: gt, lt
  Comparator #(.width(3), .mode("unsigned")) comparator_14 (
    .a(Instructions[14:12]), .b(3'b001), .eq(comparator_14_eq));  // open: gt, lt
  Comparator #(.width(3), .mode("unsigned")) comparator_15 (
    .a(Instructions[14:12]), .b(3'b010), .eq(comparator_15_eq));  // open: gt, lt
  Comparator #(.width(3), .mode("unsigned")) comparator_16 (
    .a(Instructions[14:12]), .b(3'b010), .eq(comparator_16_eq));  // open: gt, lt
  Multiplexer #(.width(4), .enable("false")) multiplexer_3 (
    .in0(multiplexer_2_out), .in1(4'b0011), .out(multiplexer_3_out), .sel(or_5_out));
  or or_5 (or_5_out, add, addi, lui, B, J, I, I);
  and and_1 (add, comparator_10_eq, R, comparator_11_eq);
  and and_2 (sll1, comparator_12_eq, R, comparator_13_eq);
  and and_3 (lh, comparator_14_eq, Ioad);
  and and_4 (slti, comparator_15_eq, Imm);
  and and_5 (MemRW, comparator_16_eq, S);
  not not_2 (BSel, R);
  Multiplexer #(.width(4), .enable("false")) multiplexer_4 (
    .in0(multiplexer_3_out), .in1(4'b0100), .out(multiplexer_4_out), .sel(sub));
  Multiplexer #(.width(4), .enable("false")) multiplexer_5 (
    .in0(multiplexer_4_out), .in1(4'b0101), .out(multiplexer_5_out), .sel(mult));
  Comparator #(.width(3), .mode("unsigned")) comparator_17 (
    .a(Instructions[14:12]), .b(3'b000), .eq(comparator_17_eq));  // open: gt, lt
  Comparator #(.width(7), .mode("unsigned")) comparator_18 (
    .a(Instructions[31:25]), .b(7'b0100000), .eq(comparator_18_eq));  // open: gt, lt
  Comparator #(.width(3), .mode("unsigned")) comparator_19 (
    .a(Instructions[14:12]), .b(3'b100), .eq(comparator_19_eq));  // open: gt, lt
  Comparator #(.width(7), .mode("unsigned")) comparator_20 (
    .a(Instructions[31:25]), .b({7{1'b0}}), .eq(comparator_20_eq));  // open: gt, lt
  Comparator #(.width(3), .mode("unsigned")) comparator_21 (
    .a(Instructions[14:12]), .b(3'b010), .eq(comparator_21_eq));  // open: gt, lt
  Comparator #(.width(3), .mode("unsigned")) comparator_22 (
    .a(Instructions[14:12]), .b(3'b100), .eq(comparator_22_eq));  // open: gt, lt
  or or_6 (ALU, Imm, R, lui, auipc);
  Multiplexer #(.width(4), .enable("false")) multiplexer_6 (
    .in0(multiplexer_5_out), .in1(4'b0110), .out(multiplexer_6_out), .sel(mulhu));
  and and_6 (sub, comparator_17_eq, R, comparator_18_eq);
  and and_7 (xor1, comparator_19_eq, R, comparator_20_eq);
  and and_8 (lw, comparator_21_eq, Ioad);
  and and_9 (xori, comparator_22_eq, Imm);
  Comparator #(.width(7), .mode("unsigned")) comparator_23 (
    .a(Instructions[31:25]), .b({7{1'b0}}), .eq(comparator_23_eq));  // open: gt, lt
  or or_7 (PCSel, beq_t, bne_t, blt_t, bgeu_t, bltu_t, J, I);
  Multiplexer #(.width(4), .enable("false")) multiplexer_7 (
    .in0(multiplexer_6_out), .in1(4'b0111), .out(multiplexer_7_out), .sel(mulh));
  Multiplexer #(.width(4), .enable("false")) multiplexer_8 (
    .in0(multiplexer_7_out), .in1(4'b1000), .out(multiplexer_8_out), .sel(divu));
  Comparator #(.width(3), .mode("unsigned")) comparator_24 (
    .a(Instructions[14:12]), .b(3'b000), .eq(comparator_24_eq));  // open: gt, lt
  Comparator #(.width(3), .mode("unsigned")) comparator_25 (
    .a(Instructions[14:12]), .b(3'b101), .eq(comparator_25_eq));  // open: gt, lt
  Multiplexer #(.width(4), .enable("false")) multiplexer_9 (
    .in0(multiplexer_8_out), .in1(4'b1001), .out(multiplexer_9_out), .sel(remu));
  Comparator #(.width(3), .mode("unsigned")) comparator_26 (
    .a(Instructions[14:12]), .b(3'b000), .eq(comparator_26_eq));  // open: gt, lt
  Comparator #(.width(7), .mode("unsigned")) comparator_27 (
    .a(Instructions[31:25]), .b(7'b0000001), .eq(comparator_27_eq));  // open: gt, lt
  Comparator #(.width(3), .mode("unsigned")) comparator_28 (
    .a(Instructions[14:12]), .b(3'b011), .eq(comparator_28_eq));  // open: gt, lt
  Comparator #(.width(7), .mode("unsigned")) comparator_29 (
    .a(Instructions[31:25]), .b({7{1'b0}}), .eq(comparator_29_eq));  // open: gt, lt
  and and_10 (srli, comparator_25_eq, comparator_23_eq, Imm);
  or or_8 (or_8_out, srl1, srli);
  and and_11 (mult, comparator_26_eq, R, comparator_27_eq);
  and and_12 (slt1, comparator_28_eq, R, comparator_29_eq);
  and and_13 (lb, comparator_24_eq, Ioad);
  Multiplexer #(.width(4), .enable("false")) multiplexer_10 (
    .in0(multiplexer_9_out), .in1(4'b1010), .out(multiplexer_10_out), .sel(or_8_out));
  or or_9 (or_9_out, Ioad, Imm);
  Multiplexer #(.width(4), .enable("false")) multiplexer_11 (
    .in0(multiplexer_10_out), .in1(4'b1011), .out(multiplexer_11_out), .sel(or_10_out));
  or or_10 (or_10_out, srai, sra1);
  or or_11 (or_11_out, sll1, slli);
  Comparator #(.width(3), .mode("unsigned")) comparator_30 (
    .a(Instructions[14:12]), .b(3'b011), .eq(comparator_30_eq));  // open: gt, lt
  Comparator #(.width(7), .mode("unsigned")) comparator_31 (
    .a(Instructions[31:25]), .b(7'b0000001), .eq(comparator_31_eq));  // open: gt, lt
  Comparator #(.width(3), .mode("unsigned")) comparator_32 (
    .a(Instructions[14:12]), .b(3'b101), .eq(comparator_32_eq));  // open: gt, lt
  Comparator #(.width(7), .mode("unsigned")) comparator_33 (
    .a(Instructions[31:25]), .b({7{1'b0}}), .eq(comparator_33_eq));  // open: gt, lt
  Comparator #(.width(3), .mode("unsigned")) comparator_34 (
    .a(Instructions[14:12]), .b(3'b100), .eq(comparator_34_eq));  // open: gt, lt
  Comparator #(.width(3), .mode("unsigned")) comparator_35 (
    .a(Instructions[14:12]), .b(3'b101), .eq(comparator_35_eq));  // open: gt, lt
  Comparator #(.width(7), .mode("unsigned")) comparator_36 (
    .a(Instructions[31:25]), .b(7'b0100000), .eq(comparator_36_eq));  // open: gt, lt
  Multiplexer #(.width(3), .enable("false")) multiplexer_12 (
    .in0(3'b000), .in1(3'b000), .out(multiplexer_12_out), .sel(or_9_out));
  Multiplexer #(.width(2), .enable("false")) multiplexer_13 (
    .in0(2'b00), .in1(2'b00), .out(multiplexer_13_out), .sel(Ioad));
  // Probe on ALUSel
  Multiplexer #(.width(4), .enable("false")) multiplexer_14 (
    .in0(multiplexer_11_out), .in1(4'b1100), .out(multiplexer_14_out), .sel(or_11_out));
  Comparator #(.width(3), .mode("unsigned")) comparator_37 (
    .a(Instructions[14:12]), .b(3'b100), .eq(comparator_37_eq));  // open: gt, lt
  and and_14 (bltu_t, bltu, BrLt);
  and and_15 (mulhu, comparator_30_eq, R, comparator_31_eq);
  and and_16 (srl1, comparator_32_eq, R, comparator_33_eq);
  and and_17 (lbu, comparator_34_eq, Ioad);
  and and_18 (srai, comparator_35_eq, Imm, comparator_36_eq);
  Comparator #(.width(3), .mode("unsigned")) comparator_38 (
    .a(Instructions[14:12]), .b(3'b110), .eq(comparator_38_eq));  // open: gt, lt
  Multiplexer #(.width(3), .enable("false")) multiplexer_15 (
    .in0(multiplexer_12_out), .in1(3'b001), .out(multiplexer_15_out), .sel(S));
  or or_12 (or_12_out, Imm, lui, R, auipc);
  Multiplexer #(.width(4), .enable("false")) multiplexer_16 (
    .in0(multiplexer_14_out), .in1(4'b1101), .out(ALUSel), .sel(or_13_out));
  or or_13 (or_13_out, slt1, slti);
  Comparator #(.width(3), .mode("unsigned")) comparator_39 (
    .a(Instructions[14:12]), .b(3'b001), .eq(comparator_39_eq));  // open: gt, lt
  and and_19 (blt, comparator_37_eq, B);
  and and_20 (bltu, comparator_38_eq, B);
  and and_21 (bne, comparator_39_eq, B);
  Multiplexer #(.width(3), .enable("false")) multiplexer_17 (
    .in0(multiplexer_15_out), .in1(3'b010), .out(multiplexer_17_out), .sel(B));
  Multiplexer #(.width(2), .enable("false")) multiplexer_18 (
    .in0(multiplexer_13_out), .in1(2'b01), .out(multiplexer_18_out), .sel(or_12_out));
  not not_3 (not_3_out, BrEq);
  and and_22 (blt_t, blt, BrLt);
  Comparator #(.width(3), .mode("unsigned")) comparator_40 (
    .a(Instructions[14:12]), .b(3'b101), .eq(comparator_40_eq));  // open: gt, lt
  Comparator #(.width(7), .mode("unsigned")) comparator_41 (
    .a(Instructions[31:25]), .b(7'b0000001), .eq(comparator_41_eq));  // open: gt, lt
  Comparator #(.width(3), .mode("unsigned")) comparator_42 (
    .a(Instructions[14:12]), .b(3'b110), .eq(comparator_42_eq));  // open: gt, lt
  Comparator #(.width(7), .mode("unsigned")) comparator_43 (
    .a(Instructions[31:25]), .b({7{1'b0}}), .eq(comparator_43_eq));  // open: gt, lt
  Comparator #(.width(3), .mode("unsigned")) comparator_44 (
    .a(Instructions[14:12]), .b(3'b101), .eq(comparator_44_eq));  // open: gt, lt
  Comparator #(.width(3), .mode("unsigned")) comparator_45 (
    .a(Instructions[14:12]), .b(3'b110), .eq(comparator_45_eq));  // open: gt, lt
  Comparator #(.width(3), .mode("unsigned")) comparator_46 (
    .a(Instructions[14:12]), .b(3'b001), .eq(comparator_46_eq));  // open: gt, lt
  Multiplexer #(.width(3), .enable("false")) multiplexer_19 (
    .in0(multiplexer_17_out), .in1(3'b100), .out(multiplexer_19_out), .sel(J));
  Multiplexer #(.width(2), .enable("false")) multiplexer_20 (
    .in0(multiplexer_18_out), .in1(2'b10), .out(WBSel), .sel(or_14_out));
  or or_14 (or_14_out, I, J);
  and and_23 (bne_t, bne, not_3_out);
  Comparator #(.width(3), .mode("unsigned")) comparator_47 (
    .a(Instructions[14:12]), .b(3'b000), .eq(comparator_47_eq));  // open: gt, lt
  and and_24 (divu, comparator_40_eq, R, comparator_41_eq);
  and and_25 (or1, comparator_42_eq, R, comparator_43_eq);
  and and_26 (lhu, comparator_44_eq, Ioad);
  and and_27 (ori, comparator_45_eq, Imm);
  Multiplexer #(.width(3), .enable("false")) multiplexer_21 (
    .in0(multiplexer_22_out), .in1(3'b101), .out(ImmSel), .sel(I));
  or or_15 (or_15_out, lui, auipc);
  and and_28 (beq, comparator_47_eq, B);
  and and_29 (bne, comparator_46_eq, B);
  Multiplexer #(.width(3), .enable("false")) multiplexer_22 (
    .in0(multiplexer_19_out), .in1(3'b011), .out(multiplexer_22_out), .sel(or_15_out));
  Comparator #(.width(3), .mode("unsigned")) comparator_48 (
    .a(Instructions[14:12]), .b(3'b111), .eq(comparator_48_eq));  // open: gt, lt
  and and_30 (beq_t, beq, BrEq);
  Comparator #(.width(3), .mode("unsigned")) comparator_49 (
    .a(Instructions[14:12]), .b(3'b111), .eq(comparator_49_eq));  // open: gt, lt
  Comparator #(.width(7), .mode("unsigned")) comparator_50 (
    .a(Instructions[31:25]), .b(7'b0000001), .eq(comparator_50_eq));  // open: gt, lt
  Comparator #(.width(3), .mode("unsigned")) comparator_51 (
    .a(Instructions[14:12]), .b(3'b111), .eq(comparator_51_eq));  // open: gt, lt
  Comparator #(.width(7), .mode("unsigned")) comparator_52 (
    .a(Instructions[31:25]), .b({7{1'b0}}), .eq(comparator_52_eq));  // open: gt, lt
  Comparator #(.width(3), .mode("unsigned")) comparator_53 (
    .a(Instructions[14:12]), .b(3'b001), .eq(comparator_53_eq));  // open: gt, lt
  Comparator #(.width(7), .mode("unsigned")) comparator_54 (
    .a(Instructions[31:25]), .b(7'b0000001), .eq(comparator_54_eq));  // open: gt, lt
  Comparator #(.width(3), .mode("unsigned")) comparator_55 (
    .a(Instructions[14:12]), .b(3'b111), .eq(comparator_55_eq));  // open: gt, lt
  and and_31 (bgeu, comparator_48_eq, B);
  and and_32 (remu, comparator_49_eq, R, comparator_50_eq);
  and and_33 (and1, comparator_51_eq, R, comparator_52_eq);
  and and_34 (mulh, comparator_53_eq, R, comparator_54_eq);
  and and_35 (andi, comparator_55_eq, Imm);
  not not_4 (not_4_out, BrLt);
  and and_36 (bgeu_t, bgeu, not_4_out);
  Comparator #(.width(3), .mode("unsigned")) comparator_56 (
    .a(Instructions[14:12]), .b(3'b101), .eq(comparator_56_eq));  // open: gt, lt
  Comparator #(.width(7), .mode("unsigned")) comparator_57 (
    .a(Instructions[31:25]), .b(7'b0100000), .eq(comparator_57_eq));  // open: gt, lt
  Comparator #(.width(3), .mode("unsigned")) comparator_58 (
    .a(Instructions[14:12]), .b(3'b000), .eq(comparator_58_eq));  // open: gt, lt
  and and_37 (sra1, comparator_56_eq, R, comparator_57_eq);
  and and_38 (addi, comparator_58_eq, Imm);
  or or_16 (or_16_out, bltu, bgeu);
  and and_39 (BrUn, or_16_out, B);
  Comparator #(.width(3), .mode("unsigned")) comparator_59 (
    .a(Instructions[14:12]), .b(3'b001), .eq(comparator_59_eq));  // open: gt, lt
  and and_40 (slli, comparator_59_eq, Imm);

  // Other names for the same wires on the sheet: ins[31:0] = Instructions; opcode[6:0] = Instructions[6:0];
  //   func3[2:0] = Instructions[14:12]; func7[6:0] = Instructions[31:25]; load = I; sw = MemRW

  // Notes on the sheet:
  //   Instruction
endmodule
