// Logisim project mem.circ as structural Verilog: 1 circuit, main circuit main
module main (
  input  [31:0] Addr,
  input  Write_enable,
  input  clock,
  input  [31:0] Write,
  output [31:0] Read
);

  RAM #(.addrWidth(14), .dataWidth(32), .trigger("falling"), .databus("bibus")) DMEM (
    .addr(Addr[13:0]), .we(Write_enable), .oe(1'b1), .clk(clock), .din(Write), .dout(Read));
endmodule
